# Fritzing sketch Robotic-Arm6DOF (saved by Fritzing 0.9.3b)

parts:
  PWM1 = PCA9685 16x12-bit PWM Breakout
  Part1 = Arduino Mega ADK (Rev3)
  J1 = Basic Servo
  J2 = Basic Servo
  J3 = Basic Servo
  J4 = Basic Servo
  J5 = Basic Servo
  J6 = Basic Servo
  U1 = POT [package=pot_alpha_rv16af-20]
  U2 = POT [package=pot_alpha_rv16af-20]
  U3 = POT [package=pot_alpha_rv16af-20]
  U4 = POT [package=pot_alpha_rv16af-20]
  U5 = POT [package=pot_alpha_rv16af-20]
  U6 = POT [package=pot_alpha_rv16af-20]
  S1 = Pushbutton [package="[SMD]"]
  S2 = Pushbutton [package="[SMD]"]
  R1 = Resistor [tolerance=±5% resistance=220 package="0805 [SMD]"]
  R2 = Resistor [tolerance=±5% resistance=220 package="0805 [SMD]"]
  SD_card_module1 = SD Card Module

nets:
  N1: PWM1.no_name_yet#0, J6.pulse
  N2: PWM1.no_name_yet#1, J3.pulse
  N3: PWM1.no_name_yet#2, J2.pulse
  N4: PWM1.no_name_yet#3, J4.pulse
  N5: PWM1.no_name_yet#4, J5.pulse
  N6: PWM1.no_name_yet#5, J1.pulse
  N7: PWM1.no_name_yet#100, PWM1.no_name_yet#101, PWM1.no_name_yet#102, PWM1.no_name_yet#103, PWM1.no_name_yet#104, PWM1.no_name_yet#105
  N8: PWM1.no_name_yet#601, PWM1.no_name_yet#1000, PWM1.no_name_yet#1001, PWM1.no_name_yet#1002, PWM1.no_name_yet#1003, PWM1.no_name_yet#1004, PWM1.no_name_yet#1005, Part1.GND, R2.Pin_1
  N9: PWM1.no_name_yet#603, Part1.D21/SCL
  N10: PWM1.no_name_yet#604, Part1.D20/SDA
  N11: PWM1.no_name_yet#605, Part1.5V
  N12: Part1.A0, U6.S
  N13: Part1.A1, U1.S
  N14: Part1.A2, U2.S
  N15: Part1.A3, U3.S
  N16: Part1.A6, U4.S
  N17: Part1.A7, U5.S
  N18: Part1.D13_PWM, R2.Pin_0
  N19: Part1.D12_PWM, R1.Pin_0
  N20: Part1.D50/MISO, SD_card_module1.MISO
  N21: Part1.D51/MOSI, SD_card_module1.MOSI
  N22: Part1.D52/SCK, SD_card_module1.SCK
  N23: Part1.D53/SS, SD_card_module1.CS
  N24: U1.A, U2.A
  N25: U1.E, U6.E
  N26: S1.Pin_3, S2.Pin_1, S2.Pin_2

custom parts:
  SD Card Module: SD Card Module Slot Socket Reader For Arduino ARM MCU
